// Logisim project 2207079.circ as structural Verilog: 1 circuit, main circuit main
module main (
  input  in_1,
  input  f1,
  input  in_3,
  input  in_4
);

  wire and_1_out, and_2_out, and_3_out, and_4_out, and_5_out, and_6_out, and_7_out, and_8_out, and_9_out,
       and_10_out, and_11_out, and_12_out, and_13_out, and_14_out, clock_1_out, d_ff_1_q, d_ff_2_q, d_ff_3_q,
       main_1_p5, main_1_p6, main_1_p7, main_1_p8, main_1_p9, main_1_p10, main_1_p11, not_1_out, not_2_out,
       not_3_out, not_4_out, not_5_out, not_6_out, or_1_out, or_2_out, or_3_out;

  not not_1 (not_1_out, in_1);
  not not_2 (not_2_out, f1);
  not not_3 (not_3_out, in_3);
  not not_4 (not_4_out, d_ff_1_q);
  not not_5 (not_5_out, d_ff_2_q);
  not not_6 (not_6_out, d_ff_3_q);
  and and_1 (and_1_out, d_ff_2_q, d_ff_3_q, in_1);
  and and_2 (and_2_out, d_ff_1_q, in_1);
  or or_1 (or_1_out, and_1_out, and_2_out);
  and and_3 (and_3_out, d_ff_3_q, f1);
  and and_4 (and_4_out, not_5_out, d_ff_3_q, in_1);
  and and_5 (and_5_out, d_ff_2_q, f1);
  and and_6 (and_6_out, d_ff_2_q, not_6_out, in_1);
  and and_7 (and_7_out, d_ff_2_q, d_ff_3_q, not_1_out);
  and and_8 (and_8_out, d_ff_1_q, not_1_out);
  and and_9 (and_9_out, not_5_out, not_6_out, f1);
  and and_10 (and_10_out, not_4_out, not_6_out, in_1);
  and and_11 (and_11_out, not_5_out, not_2_out, in_3);
  and and_12 (and_12_out, d_ff_2_q, not_6_out, not_2_out);
  and and_13 (and_13_out, d_ff_2_q, f1, in_3);
  and and_14 (and_14_out, d_ff_1_q, not_1_out);
  D_Flip_Flop d_ff_1 (.clk(clock_1_out), .D(or_1_out), .Q(d_ff_1_q));  // open: Qn, preset, en, reset
  or or_2 (or_2_out, and_3_out, and_4_out, and_5_out, and_6_out, and_7_out, and_8_out);
  or or_3 (or_3_out, and_9_out, and_10_out, and_11_out, and_12_out, and_13_out, and_14_out);
  D_Flip_Flop d_ff_2 (.clk(clock_1_out), .D(or_2_out), .Q(d_ff_2_q));  // open: Qn, preset, en, reset
  D_Flip_Flop d_ff_3 (.clk(clock_1_out), .D(or_3_out), .Q(d_ff_3_q));  // open: Qn, preset, en, reset
  Clock clock_1 (.out(clock_1_out));
  // _7_segment_main main_1: pin names not known; wires that end beside it: in_4, d_ff_1_q, d_ff_2_q, d_ff_3_q, main_1_p5, main_1_p6, main_1_p7, main_1_p8, main_1_p9, main_1_p10, main_1_p11
  _7_Segment_Display u_7_segment_display_1 (
    .g(main_1_p11), .f(main_1_p10), .a(main_1_p5), .b(main_1_p6), .e(main_1_p9), .d(main_1_p8), .c(main_1_p7));  // open: dp

  // Notes on the sheet:
  //   f2
  //   f0
  //   q2
  //   q1
  //   q0
  //   2207079
endmodule
